# Fritzing sketch ProjectSchematic (saved by Fritzing 0.9.5d)
breadboards: 1

parts:
  U1_ESP32 = ESP32 Dev_Kit
  U2_NEO-6M_GPS = u-blox NEO-6M GPS Breakout
  U3_MPU6050 = InvenSense MPU6050
  U4_SIM800L = SIM800L GSM module (bare)
  PSU1_Buck_4_0V = Buck converter 4.0 V (MP1584 / LM2596)
  C1_1000uF = Electrolytic Capacitor [capacitance=1000ÂµF voltage=16V package="100 mil [THT, electrolytic]"]
  R1_10k = Resistor [resistance=10kÎ© package=THT]
  R2_20k = Resistor [resistance=20kÎ© package=THT]
  R3_1k = Resistor [resistance=1kÎ© package=THT]
  Q1_2N2222 = NPN-Transistor [package="TO92 [THT]"]
  BZ1_Buzzer = Piezo Speaker

nets:
  N1: U1_ESP32.3.3, U2_NEO-6M_GPS.Pin_1, U3_MPU6050.VCC
  N2: U1_ESP32.GPIO25, R3_1k.Pin_1
  N3: U1_ESP32.GPIO26, U4_SIM800L.TXD
  N4: U1_ESP32.GPIO27, R1_10k.Pin_1
  GND: U1_ESP32.GND, U2_NEO-6M_GPS.Pin_2, U3_MPU6050.GND, U3_MPU6050.AD0, U4_SIM800L.GND, PSU1_Buck_4_0V.OUT-, C1_1000uF.-, R2_20k.Pin_1, Q1_2N2222.E
  N5: U1_ESP32.VIN, BZ1_Buzzer.pin1
  N6: U1_ESP32.GPIO4, U4_SIM800L.RST
  N7: U1_ESP32.GPIO16, U2_NEO-6M_GPS.Pin_3
  N8: U1_ESP32.GPIO17, U2_NEO-6M_GPS.Pin_4
  N9: U1_ESP32.GPIO21, U3_MPU6050.SDA
  N10: U1_ESP32.GPIO22, U3_MPU6050.SCL
  N11: U4_SIM800L.VCC, PSU1_Buck_4_0V.OUT+, C1_1000uF.+
  N12: U4_SIM800L.RXD, R1_10k.Pin_0, R2_20k.Pin_0
  N13: R3_1k.Pin_0, Q1_2N2222.B
  N14: Q1_2N2222.C, BZ1_Buzzer.pin2

custom parts:
  SIM800L GSM module (bare): Bare SIM800L quad-band GSM/GPRS module. Supply 3.4-4.4 V with 2 A peaks. UART at 2.8 V logic.
  Buck converter 4.0 V (MP1584 / LM2596): Step-down converter module. Set the output to 4.0 V with a multimeter before connecting the SIM800L. Input 5-12 V. IN- and OUT- are the same ground.
